# Fritzing sketch ir senser & receiver (saved by Fritzing 0.9.3b)
breadboards: 1

parts:
  Part1 = Arduino Uno (Rev3) - ICSP
  IR1 = TSOP312.., 314.. [package=THT]
  M2 = fc-51 [package=THT]

nets:
  N1: Part1.D4, IR1.Data
  N2: Part1.D5_PWM, M2.pin1
  N3: Part1.5V, IR1.Vs, M2.pin3
  GND: Part1.GND, IR1.GND, M2.pin2
