# Fritzing sketch lcd (saved by Fritzing 0.9.3b)

parts:
  LCD2004-I2C1 = LCD2004-I2C  # not connected
  LCM1602_IIC1 = LCM1602 IIC [part_number="LCM1602 IIC" chip_label="LCM1602 IIC" package="DIP (Dual Inline) [THT]"]
  Part1 = Arduino Uno (Rev3) - ICSP

nets:
  GND: LCM1602_IIC1.GND, Part1.GND
  VCC: LCM1602_IIC1.VCC, Part1.5V
  N1: LCM1602_IIC1.SDA, Part1.A4/SDA
  N2: LCM1602_IIC1.SCL, Part1.A5/SCL

custom parts:
  LCD2004-I2C: A standard character display with 4x20 characters. Comes in many colors with LCM2004 IIC attached.
  LCM1602 IIC: I2C-Module to use a 1602 or 2004 LCD on with the wire.h libory Serial LCD Modul
