# Fritzing sketch servo motor (saved by Fritzing 0.9.3b)

parts:
  J2 = Basic Servo
  Part1 = Arduino Uno (Rev3) - ICSP

nets:
  GND: J2.gnd, Part1.GND
  VCC: J2.vcc, Part1.5V
  N1: J2.pulse, Part1.D7
