# Fritzing sketch led+wifi (saved by Fritzing 0.9.3b)
breadboards: 1

parts:
  Part1 = Arduino Uno (Rev3) - ICSP
  LED1 = smd LED [color="Red (633nm)" package="0603 [SMD]"]
  LED2 = smd LED [color="Red (633nm)" package="0603 [SMD]"]
  LED4 = smd LED [color="Red (633nm)" package="0603 [SMD]"]
  LED5 = smd LED [color="Red (633nm)" package="0603 [SMD]"]
  LED6 = smd LED [color="Red (633nm)" package="0603 [SMD]"]
  LED7 = smd LED [color="Green (555nm)" package="0603 [SMD]"]
  LED8 = smd LED [color="Green (555nm)" package="0603 [SMD]"]
  LED9 = smd LED [color="Green (555nm)" package="0603 [SMD]"]
  LED10 = smd LED [color="Green (555nm)" package="0603 [SMD]"]
  LED11 = smd LED [color="Green (555nm)" package="0603 [SMD]"]
  LED12 = smd LED [color="Green (555nm)" package="0603 [SMD]"]
  LED3 = smd LED [color="Red (633nm)" package="0603 [SMD]"]
  U1 = ESP8266 WiFi Module [part_number=ESP8266]

nets:
  N1: Part1.D8, LED9.anode
  N2: Part1.D9_PWM, LED3.anode
  N3: Part1.D10_PWM/SS, LED8.anode
  N4: Part1.D11_PWM/MOSI, LED2.anode
  N5: Part1.D13/SCK, LED1.anode
  GND: Part1.GND, LED1.cathode, LED2.cathode, LED4.cathode, LED5.cathode, LED6.cathode, LED6.anode, LED7.cathode, LED8.cathode, LED9.cathode, LED10.cathode, LED11.cathode, LED12.cathode, LED3.cathode, U1.GND
  N6: Part1.D0/RX, U1.TXD
  N7: Part1.D1/TX, U1.RXD
  N8: Part1.D2, LED12.anode
  N9: Part1.D4, LED11.anode
  N10: Part1.D5_PWM, LED5.anode
  N11: Part1.D6_PWM, LED10.anode
  N12: Part1.D7, LED4.anode
  5V: Part1.5V, U1.VCC

custom parts:
  ESP8266 WiFi Module: Generic WiFi Module based on the ESP8266 with onboard PCB antenna and UART communications
