# Fritzing sketch led (saved by Fritzing 0.9.3b)
breadboards: 1

parts:
  LED1 = smd LED [color="Green (555nm)" package="0603 [SMD]"]
  Part1 = Arduino Uno (Rev3) - ICSP
  R1 = Resistor [tolerance=±5% resistance=220 package="2010 [SMD]"]
  R2 = Resistor [tolerance=±5% resistance=220 package="2010 [SMD]"]
  LED2 = smd LED [color="Red (633nm)" package="0805 [SMD]"]

nets:
  N1: LED1.cathode, Part1.GND, LED2.cathode
  N2: LED1.anode, R2.Pin_0
  N3: Part1.D6_PWM, R1.Pin_1
  N4: Part1.D7, R2.Pin_1
  N5: R1.Pin_0, LED2.anode
