# Fritzing sketch project illuminate (saved by Fritzing 0.9.3b)
breadboards: 1

parts:
  LCM1602_IIC1 = LCM1602 IIC [part_number="LCM1602 IIC" chip_label="LCM1602 IIC" package="DIP (Dual Inline) [THT]"]
  LCD2004-I2C1 = LCD2004-I2C  # not connected
  Part1 = Arduino Uno (Rev3) - ICSP
  M1 = fc-51 [package=THT]
  M2 = fc-51 [package=THT]
  LED1 = smd LED [color="Green (555nm)" package="0603 [SMD]"]
  LED2 = smd LED [color="Red (633nm)" package="0603 [SMD]"]
  LED4 = smd LED [color="Red (633nm)" package="0603 [SMD]"]
  IR1 = TSOP312.., 314.. [package=THT]
  LED3 = smd LED [color="Green (555nm)" package="1206 [SMD]"]
  J3 = Basic Servo
  J2 = Basic Servo

nets:
  GND: LCM1602_IIC1.GND, Part1.GND, M1.pin2, M2.pin2, LED1.cathode, LED2.cathode, LED4.cathode, IR1.GND, LED3.cathode, J3.gnd, J2.gnd
  VCC: LCM1602_IIC1.VCC, Part1.5V, M1.pin3, M2.pin3, IR1.Vs, J3.vcc, J2.vcc
  N1: LCM1602_IIC1.SDA, Part1.A4/SDA
  N2: LCM1602_IIC1.SCL, Part1.A5/SCL
  N3: Part1.D8, LED3.anode
  N4: Part1.D9_PWM, LED2.anode
  N5: Part1.D10_PWM/SS, LED4.anode
  N6: Part1.D2, IR1.Data
  N7: Part1.D3_PWM, M2.pin1
  N8: Part1.D4, M1.pin1
  N9: Part1.D5_PWM, J3.pulse
  N10: Part1.D6_PWM, J2.pulse
  N11: Part1.D7, LED1.anode

custom parts:
  LCM1602 IIC: I2C-Module to use a 1602 or 2004 LCD on with the wire.h libory Serial LCD Modul
  LCD2004-I2C: A standard character display with 4x20 characters. Comes in many colors with LCM2004 IIC attached.
